// Logisim project 1 bit ALU.circ as structural Verilog: 1 circuit, main circuit main
module main (
  input  [1:0] ALU_opcode,
  input  A,
  input  B,
  input  Cin_Bin,
  output Output,
  output Cout_Bout
);

  wire adder_1_cout, adder_1_out, and_1_out, or_1_out, subtractor_1_bout, subtractor_1_out;

  and and_1 (and_1_out, A, B);
  or or_1 (or_1_out, A, B);
  Adder #(.width(1)) adder_1 (.a(A), .b(B), .out(adder_1_out), .cin(Cin_Bin), .cout(adder_1_cout));
  Subtractor #(.width(1)) subtractor_1 (.a(A), .b(B), .out(subtractor_1_out), .bin(Cin_Bin), .bout(subtractor_1_bout));
  Multiplexer #(.select(2), .enable("false")) multiplexer_1 (
    .in0(and_1_out), .in1(or_1_out), .in2(adder_1_out), .in3(subtractor_1_out), .out(Output), .sel(ALU_opcode));
  Multiplexer #(.enable("false")) multiplexer_2 (
    .in0(adder_1_cout), .in1(subtractor_1_bout), .out(Cout_Bout), .sel(ALU_opcode[0]));
endmodule
