// Logisim project 12 bit ALU.circ as structural Verilog: 1 circuit, main circuit main
module main (
  input  [1:0] ALU_Opcode,
  input  [11:0] A,
  input  [11:0] B,
  input  Zero,
  output Zero_Signal,
  output [11:0] Output
);

  wire main_1_cout_bout, main_2_cout_bout, main_3_cout_bout, not_1_out, or_2_out;
  wire [3:0] or_1_out;

  _4_bit_ALU_main main_1 (
    .Cin_Bin(1'b0), .ALU_Opcode(ALU_Opcode), .A(A[3:0]), .B(B[3:0]), .Output(Output[3:0]),
    .Cout_Bout(main_1_cout_bout));
  _4_bit_ALU_main main_2 (
    .Cin_Bin(main_1_cout_bout), .ALU_Opcode(ALU_Opcode), .A(A[7:4]), .B(B[7:4]), .Output(Output[7:4]),
    .Cout_Bout(main_2_cout_bout));
  _4_bit_ALU_main main_3 (
    .Cin_Bin(main_2_cout_bout), .ALU_Opcode(ALU_Opcode), .A(A[11:8]), .B(B[11:8]), .Output(Output[11:8]),
    .Cout_Bout(main_3_cout_bout));
  assign or_1_out = Output[3:0] | Output[7:4] | Output[11:8];  // OR_Gate or_1, 4 bits wide
  or or_2 (or_2_out, or_1_out[0], or_1_out[1], or_1_out[2], or_1_out[3], main_3_cout_bout);
  not not_1 (not_1_out, or_2_out);
  Multiplexer #(.enable("false")) multiplexer_1 (
    .in0(main_3_cout_bout), .in1(not_1_out), .out(Zero_Signal), .sel(Zero));
endmodule
