// Logisim project 4 bit ALU.circ as structural Verilog: 1 circuit, main circuit main
module main (
  input  Cin_Bin,
  input  [1:0] ALU_Opcode,
  input  [3:0] A,
  input  [3:0] B,
  output [3:0] Output,
  output Cout_Bout
);

  wire main_1_cout_bout, main_2_cout_bout, main_3_cout_bout;

  _1_bit_ALU_main main_1 (
    .ALU_opcode(ALU_Opcode), .A(A[0]), .B(B[0]), .Cin_Bin(Cin_Bin), .Output(Output[0]),
    .Cout_Bout(main_1_cout_bout));
  _1_bit_ALU_main main_2 (
    .ALU_opcode(ALU_Opcode), .A(A[1]), .B(B[1]), .Cin_Bin(main_1_cout_bout), .Output(Output[1]),
    .Cout_Bout(main_2_cout_bout));
  _1_bit_ALU_main main_3 (
    .ALU_opcode(ALU_Opcode), .A(A[2]), .B(B[2]), .Cin_Bin(main_2_cout_bout), .Output(Output[2]),
    .Cout_Bout(main_3_cout_bout));
  _1_bit_ALU_main main_4 (
    .ALU_opcode(ALU_Opcode), .A(A[3]), .B(B[3]), .Cin_Bin(main_3_cout_bout), .Output(Output[3]),
    .Cout_Bout(Cout_Bout));
endmodule
