// Logisim project ALU-Opcode.circ as structural Verilog: 1 circuit, main circuit main
module main (
  input  [3:0] Opcode,
  output [2:0] ALU_Opcode
);

  wire and_2_out, and_3_out, and_4_out, and_5_out, not_1_out, not_2_out, not_3_out, not_4_out, not_5_out,
       not_6_out;

  not not_1 (not_1_out, Opcode[1]);
  not not_2 (not_2_out, Opcode[2]);
  not not_3 (not_3_out, Opcode[1]);
  not not_4 (not_4_out, Opcode[0]);
  not not_5 (not_5_out, Opcode[3]);
  not not_6 (not_6_out, Opcode[1]);
  and and_1 (ALU_Opcode[2], Opcode[2], not_1_out, Opcode[0]);
  and and_2 (and_2_out, not_2_out, not_3_out);
  and and_3 (and_3_out, Opcode[1], not_4_out);
  and and_4 (and_4_out, Opcode[2], Opcode[1]);
  and and_5 (and_5_out, not_5_out, not_6_out, Opcode[0]);
  or or_1 (ALU_Opcode[1], and_2_out, and_3_out, and_4_out);
  or or_2 (ALU_Opcode[0], and_5_out, Opcode[2]);
endmodule
