// Logisim project ALU.circ as structural Verilog: 1 circuit, main circuit main
module main (
  input  [2:0] ALU_Opcode,
  input  [11:0] A,
  input  [11:0] B,
  input  Zero_Signal,
  output Zero_Signal_2,
  output [11:0] Output
);

  wire [11:0] main_1_output, shifter_1_out;

  _12_bit_ALU_main main_1 (
    .ALU_Opcode(ALU_Opcode[1:0]), .A(A), .B(B), .Zero(Zero_Signal), .Zero_Signal(Zero_Signal_2),
    .Output(main_1_output));
  Shifter #(.width(12)) shifter_1 (.in(A), .\dist (B[3:0]), .out(shifter_1_out));
  Multiplexer #(.width(12), .enable("false")) multiplexer_1 (
    .in0(main_1_output), .in1(shifter_1_out), .out(Output), .sel(ALU_Opcode[2]));
endmodule
