// Logisim project Control Unit.circ as structural Verilog: 1 circuit, main circuit main
module main (
  input  [3:0] Opcode,
  output [2:0] ALU_Opcode,
  output Write_Register,
  output [1:0] Branch,
  output [1:0] Write_Read_Memory,
  output Zero_Signal,
  output [1:0] Output,
  output First_Oprand,
  output [1:0] Second_Operand
);

  wire and_1_out, and_2_out, and_3_out, and_4_out, and_6_out, and_7_out, and_9_out, and_10_out, not_1_out,
       not_2_out, not_3_out, not_4_out, not_5_out, not_6_out, not_7_out, not_8_out, not_9_out, not_10_out,
       not_11_out, not_12_out, not_15_out, not_16_out, not_17_out, not_18_out;

  ALU_Opcode_main main_1 (.Opcode(Opcode), .ALU_Opcode(ALU_Opcode));
  not not_1 (not_1_out, Opcode[3]);
  and and_1 (and_1_out, not_1_out, not_2_out);
  not not_2 (not_2_out, Opcode[2]);
  not not_3 (not_3_out, Opcode[3]);
  and and_2 (and_2_out, not_3_out, not_4_out);
  not not_4 (not_4_out, Opcode[1]);
  not not_5 (not_5_out, Opcode[3]);
  and and_3 (and_3_out, not_5_out, Opcode[0]);
  not not_6 (not_6_out, Opcode[1]);
  and and_4 (and_4_out, not_6_out, Opcode[0]);
  not not_7 (not_7_out, Opcode[2]);
  not not_8 (not_8_out, Opcode[1]);
  not not_9 (not_9_out, Opcode[0]);
  and and_5 (Branch[0], Opcode[2], Opcode[1], not_10_out);
  not not_10 (not_10_out, Opcode[0]);
  not not_11 (not_11_out, Opcode[1]);
  and and_6 (and_6_out, Opcode[3], not_11_out, Opcode[0]);
  and and_7 (and_7_out, Opcode[3], Opcode[1], not_12_out);
  not not_12 (not_12_out, Opcode[0]);
  not not_13 (Write_Read_Memory[0], Opcode[1]);
  not not_14 (Zero_Signal, Opcode[0]);
  and and_8 (Output[0], Opcode[2], Opcode[1]);
  not not_15 (not_15_out, Opcode[2]);
  and and_9 (and_9_out, not_15_out, Opcode[1], not_16_out);
  not not_16 (not_16_out, Opcode[0]);
  and and_10 (and_10_out, Opcode[2], not_17_out, Opcode[0]);
  not not_17 (not_17_out, Opcode[1]);
  and and_11 (Second_Operand[0], Opcode[1], not_18_out);
  not not_18 (not_18_out, Opcode[0]);
  or or_1 (Write_Register, and_1_out, and_2_out, and_3_out, and_4_out);
  and and_12 (Branch[1], Opcode[3], not_7_out, not_8_out, not_9_out);
  or or_2 (Write_Read_Memory[1], and_6_out, and_7_out);
  or or_3 (Second_Operand[1], and_9_out, and_10_out, Opcode[3]);

  assign First_Oprand = Opcode[3];
  assign Output[1] = Opcode[3];
endmodule
