// Logisim project Datapath.circ as structural Verilog: 6 circuits, main circuit main
module main (
  input  [11:0] in_1,
  output [11:0] A,
  output [11:0] B,
  output [11:0] Y,
  output [11:0] WB,
  output [2:0] out_6,
  output [3:0] OP,
  output [3:0] RS,
  output [3:0] RT
);

  wire ALUSrc, and_1_out, Binvert, CLK, lw_sw, MR, MTR, MW, n12bit_1_zero, PCSrc, RW, Sll;
  wire [11:0] adder_1_out, adder_2_out, Level, multiplexer_2_out, ram_1_data, regfile_1_b, register_1_q;

  Clock clock_1 (.out(CLK));
  Register #(.width(12)) register_1 (.D(multiplexer_2_out), .Q(register_1_q), .clk(CLK));  // open: en, clr
  Adder #(.width(12)) adder_1 (.a(in_1), .b(register_1_q), .out(adder_1_out));  // open: cin, cout
  ROM #(.addrWidth(12), .dataWidth(12)) rom_1 (.addr(register_1_q), .data({OP, RS, RT}));  // open: sel
  assign Level = {{8{1'b0}}, RT};  // Bit_Extender bit_extender_1
  regfile regfile_1 (
    .RegWrite(RW), .Input(WB), .DecodeControl(RS), .MuxAControl(RS), .MuxBControl(RT), .A(A),
    .B(regfile_1_b), .Clock(CLK), .Beq(PCSrc));
  Control control_1 (
    .in_1(OP), .PCSrc(PCSrc), .RegWrite(RW), .ALUSrc(ALUSrc), .MemoryWrite(MW), .MemoryRead(MR),
    .MemToReg(MTR), .Sll(Sll), .Binvert(Binvert), .Lw_Sw(lw_sw), .out_11(out_6));
  Multiplexer #(.width(12), .enable("false")) multiplexer_1 (.in0(regfile_1_b), .in1(Level), .out(B), .sel(ALUSrc));
  Adder #(.width(12)) adder_2 (.a(adder_1_out), .b(Level), .out(adder_2_out));  // open: cin, cout
  _12bit u_12bit_1 (
    .A(A), .B(B), .Lw_Sw(lw_sw), .ControlBit(out_6), .Binverter(Binvert), .ShiftLeft(Sll), .Y(Y),
    .Zero(n12bit_1_zero));  // open: Cout
  and and_1 (and_1_out, PCSrc, n12bit_1_zero);
  Multiplexer #(.width(12), .enable("false")) multiplexer_2 (
    .in0(adder_1_out), .in1(adder_2_out), .out(multiplexer_2_out), .sel(and_1_out));
  RAM #(.addrWidth(12), .dataWidth(12), .bus("separate")) ram_1 (
    .addr(Y), .data(ram_1_data), .str(MW), .clk(CLK), .ld(MR));  // open: din, sel, clr
  Multiplexer #(.width(12), .enable("false")) multiplexer_3 (.in0(ram_1_data), .in1(Y), .out(WB), .sel(MTR));

  // Other names for the same wires on the sheet: ALUOP[2:0] = out_6

  // Notes on the sheet:
  //   contents of rom_1 (hex, n*v repeats v):
  //   1 101 1 10 b72 233 0 cb2
endmodule

module ALU (
  input  A,
  input  B,
  input  Cin,
  input  Binverter,
  input  slt,
  input  [2:0] ALUcontrolbit,
  output Y,
  output Cout,
  output Set
);

  wire and_1_out, multiplexer_1_out, not_1_out, or_1_out;

  Multiplexer #(.enable("false")) multiplexer_1 (.in0(B), .in1(not_1_out), .out(multiplexer_1_out), .sel(Binverter));
  not not_1 (not_1_out, B);
  Adder #(.width(1)) adder_1 (.a(A), .b(multiplexer_1_out), .out(Set), .cin(Cin), .cout(Cout));
  and and_1 (and_1_out, A, B);
  or or_1 (or_1_out, A, B);
  Multiplexer #(.select(3), .enable("false")) multiplexer_2 (
    .in0(Set), .in1(Set), .in2(and_1_out), .in3(or_1_out), .in4(slt), .out(Y), .sel(ALUcontrolbit));  // open: in5, in6, in7
endmodule

module _12bit (
  input  [11:0] A,
  input  [11:0] B,
  input  Lw_Sw,
  input  [2:0] ControlBit,
  input  Binverter,
  input  ShiftLeft,
  output [11:0] Y,
  output Zero,
  output Cout
);

  wire alu_1_cout, alu_2_cout, alu_3_cout, alu_4_cout, alu_5_cout, alu_6_cout, alu_7_cout, alu_8_cout,
       alu_9_cout, alu_10_cout, alu_11_cout, alu_12_set;
  wire [11:0] adder_1_out, alu_1_y, multiplexer_1_out, register_1_q, shifter_1_out, shifter_2_out;

  Register #(.width(12)) register_1 (.Q(register_1_q));  // open: D, en, clk, clr
  ALU alu_1 (
    .Binverter(Binverter), .slt(alu_12_set), .ALUcontrolbit(ControlBit), .Y(alu_1_y[0]), .A(A[0]), .B(B[0]),
    .Cin(Binverter), .Cout(alu_1_cout));  // open: Set
  ALU alu_2 (
    .Binverter(Binverter), .slt(1'b0), .ALUcontrolbit(ControlBit), .Y(alu_1_y[1]), .A(A[1]), .B(B[1]),
    .Cin(alu_1_cout), .Cout(alu_2_cout));  // open: Set
  ALU alu_3 (
    .Binverter(Binverter), .slt(1'b0), .ALUcontrolbit(ControlBit), .Y(alu_1_y[2]), .A(A[2]), .B(B[2]),
    .Cin(alu_2_cout), .Cout(alu_3_cout));  // open: Set
  ALU alu_4 (
    .Binverter(Binverter), .slt(1'b0), .ALUcontrolbit(ControlBit), .Y(alu_1_y[3]), .A(A[3]), .B(B[3]),
    .Cin(alu_3_cout), .Cout(alu_4_cout));  // open: Set
  ALU alu_5 (
    .Binverter(Binverter), .slt(1'b0), .ALUcontrolbit(ControlBit), .Y(alu_1_y[4]), .A(A[4]), .B(B[4]),
    .Cin(alu_4_cout), .Cout(alu_5_cout));  // open: Set
  ALU alu_6 (
    .Binverter(Binverter), .slt(1'b0), .ALUcontrolbit(ControlBit), .Y(alu_1_y[5]), .A(A[5]), .B(B[5]),
    .Cin(alu_5_cout), .Cout(alu_6_cout));  // open: Set
  ALU alu_7 (
    .Binverter(Binverter), .slt(1'b0), .ALUcontrolbit(ControlBit), .Y(alu_1_y[6]), .A(A[6]), .B(B[6]),
    .Cin(alu_6_cout), .Cout(alu_7_cout));  // open: Set
  ALU alu_8 (
    .Binverter(Binverter), .slt(1'b0), .ALUcontrolbit(ControlBit), .Y(alu_1_y[7]), .A(A[7]), .B(B[7]),
    .Cin(alu_7_cout), .Cout(alu_8_cout));  // open: Set
  ALU alu_9 (
    .Binverter(Binverter), .slt(1'b0), .ALUcontrolbit(ControlBit), .Y(alu_1_y[8]), .A(A[8]), .B(B[8]),
    .Cin(alu_8_cout), .Cout(alu_9_cout));  // open: Set
  ALU alu_10 (
    .Binverter(Binverter), .slt(1'b0), .ALUcontrolbit(ControlBit), .Y(alu_1_y[9]), .A(A[9]), .B(B[9]),
    .Cin(alu_9_cout), .Cout(alu_10_cout));  // open: Set
  ALU alu_11 (
    .Binverter(Binverter), .slt(1'b0), .ALUcontrolbit(ControlBit), .Y(alu_1_y[10]), .A(A[10]), .B(B[10]),
    .Cin(alu_10_cout), .Cout(alu_11_cout));  // open: Set
  ALU alu_12 (
    .Binverter(Binverter), .slt(1'b0), .ALUcontrolbit(ControlBit), .Y(alu_1_y[11]), .A(A[11]), .B(B[11]),
    .Cin(alu_11_cout), .Cout(Cout), .Set(alu_12_set));
  Shifter #(.width(12)) shifter_1 (.in(B), .\dist (4'b0010), .out(shifter_1_out));
  Adder #(.width(12)) adder_1 (.a(register_1_q), .b(shifter_1_out), .out(adder_1_out));  // open: cin, cout
  Shifter #(.width(12)) shifter_2 (.in(A), .\dist (B[3:0]), .out(shifter_2_out));
  Multiplexer #(.width(12), .enable("false")) multiplexer_1 (
    .in0(alu_1_y), .in1(shifter_2_out), .out(multiplexer_1_out), .sel(ShiftLeft));
  Multiplexer #(.width(12), .enable("false")) multiplexer_2 (
    .in0(multiplexer_1_out), .in1(adder_1_out), .out(Y), .sel(Lw_Sw));
  nor nor_1 (Zero, alu_1_y[0], alu_1_y[1], alu_1_y[2], alu_1_y[3], alu_1_y[4], alu_1_y[5], alu_1_y[6], alu_1_y[7], alu_1_y[8], alu_1_y[9], alu_1_y[10], alu_1_y[11]);
endmodule

module regfile (
  input  RegWrite,
  input  [11:0] Input,
  input  Clock,
  input  [3:0] DecodeControl,
  input  [3:0] MuxAControl,
  input  [3:0] MuxBControl,
  input  Beq,
  output [11:0] A,
  output [11:0] B
);

  wire and_1_out, and_2_out, and_3_out, and_4_out, and_5_out, and_6_out, and_7_out, and_8_out, and_9_out,
       and_10_out, and_11_out, and_12_out, and_13_out, and_14_out, and_15_out, and_16_out, decoder_1_out0,
       decoder_1_out1, decoder_1_out2, decoder_1_out3, decoder_1_out4, decoder_1_out5, decoder_1_out6,
       decoder_1_out7, decoder_1_out8, decoder_1_out9, decoder_1_out10, decoder_1_out11, decoder_1_out12,
       decoder_1_out13, decoder_1_out14, decoder_1_out15;
  wire [3:0] multiplexer_1_out, register_1_q;
  wire [11:0] register_2_q, register_3_q, register_4_q, register_5_q, register_6_q, register_7_q,
       register_8_q, register_9_q, register_10_q, register_11_q, register_12_q, register_13_q, register_14_q,
       register_15_q, register_16_q, register_17_q;

  Register #(.width(4)) register_1 (.Q(register_1_q));  // open: D, en, clk, clr
  Multiplexer #(.width(4), .enable("false")) multiplexer_1 (
    .in0(MuxBControl), .in1(register_1_q), .out(multiplexer_1_out), .sel(Beq));
  Decoder #(.select(4), .enable("false")) decoder_1 (
    .out0(decoder_1_out0), .out1(decoder_1_out1), .out2(decoder_1_out2), .out3(decoder_1_out3),
    .out4(decoder_1_out4), .out5(decoder_1_out5), .out6(decoder_1_out6), .out7(decoder_1_out7),
    .out8(decoder_1_out8), .out9(decoder_1_out9), .out10(decoder_1_out10), .out11(decoder_1_out11),
    .out12(decoder_1_out12), .out13(decoder_1_out13), .out14(decoder_1_out14), .out15(decoder_1_out15),
    .sel(DecodeControl));
  and and_1 (and_1_out, RegWrite, decoder_1_out0);
  and and_2 (and_2_out, RegWrite, decoder_1_out1);
  and and_3 (and_3_out, RegWrite, decoder_1_out2);
  and and_4 (and_4_out, RegWrite, decoder_1_out3);
  and and_5 (and_5_out, RegWrite, decoder_1_out4);
  and and_6 (and_6_out, RegWrite, decoder_1_out5);
  and and_7 (and_7_out, RegWrite, decoder_1_out6);
  and and_8 (and_8_out, RegWrite, decoder_1_out7);
  and and_9 (and_9_out, RegWrite, decoder_1_out8);
  and and_10 (and_10_out, RegWrite, decoder_1_out9);
  and and_11 (and_11_out, RegWrite, decoder_1_out10);
  and and_12 (and_12_out, RegWrite, decoder_1_out11);
  and and_13 (and_13_out, RegWrite, decoder_1_out12);
  and and_14 (and_14_out, RegWrite, decoder_1_out13);
  and and_15 (and_15_out, RegWrite, decoder_1_out14);
  and and_16 (and_16_out, RegWrite, decoder_1_out15);
  Register #(.width(12)) register_2 (.D(Input), .en(and_1_out), .Q(register_2_q), .clk(Clock));  // open: clr
  Register #(.width(12)) register_3 (.D(Input), .en(and_2_out), .Q(register_3_q), .clk(Clock));  // open: clr
  Register #(.width(12)) register_4 (.D(Input), .en(and_3_out), .Q(register_4_q), .clk(Clock));  // open: clr
  Register #(.width(12)) register_5 (.D(Input), .en(and_4_out), .Q(register_5_q), .clk(Clock));  // open: clr
  Register #(.width(12)) register_6 (.D(Input), .en(and_5_out), .Q(register_6_q), .clk(Clock));  // open: clr
  Register #(.width(12)) register_7 (.D(Input), .en(and_6_out), .Q(register_7_q), .clk(Clock));  // open: clr
  Register #(.width(12)) register_8 (.D(Input), .en(and_7_out), .Q(register_8_q), .clk(Clock));  // open: clr
  Register #(.width(12)) register_9 (.D(Input), .en(and_8_out), .Q(register_9_q), .clk(Clock));  // open: clr
  Register #(.width(12)) register_10 (.D(Input), .en(and_9_out), .Q(register_10_q), .clk(Clock));  // open: clr
  Register #(.width(12)) register_11 (.D(Input), .en(and_10_out), .Q(register_11_q), .clk(Clock));  // open: clr
  Register #(.width(12)) register_12 (.D(Input), .en(and_11_out), .Q(register_12_q), .clk(Clock));  // open: clr
  Register #(.width(12)) register_13 (.D(Input), .en(and_12_out), .Q(register_13_q), .clk(Clock));  // open: clr
  Register #(.width(12)) register_14 (.D(Input), .en(and_13_out), .Q(register_14_q), .clk(Clock));  // open: clr
  Register #(.width(12)) register_15 (.D(Input), .en(and_14_out), .Q(register_15_q), .clk(Clock));  // open: clr
  Register #(.width(12)) register_16 (.D(Input), .en(and_15_out), .Q(register_16_q), .clk(Clock));  // open: clr
  Register #(.width(12)) register_17 (.D(Input), .en(and_16_out), .Q(register_17_q), .clk(Clock));  // open: clr
  Multiplexer #(.select(4), .width(12), .enable("false")) multiplexer_2 (
    .in0(register_2_q), .in1(register_3_q), .in2(register_4_q), .in3(register_5_q), .in4(register_6_q),
    .in5(register_7_q), .in6(register_8_q), .in7(register_9_q), .in8(register_10_q), .in9(register_11_q),
    .in10(register_12_q), .in11(register_13_q), .in12(register_14_q), .in13(register_15_q),
    .in14(register_16_q), .in15(register_17_q), .out(A), .sel(MuxAControl));
  Multiplexer #(.select(4), .width(12), .enable("false")) multiplexer_3 (
    .in0(register_2_q), .in1(register_3_q), .in2(register_4_q), .in3(register_5_q), .in4(register_6_q),
    .in5(register_7_q), .in6(register_8_q), .in7(register_9_q), .in8(register_10_q), .in9(register_11_q),
    .in10(register_12_q), .in11(register_13_q), .in12(register_14_q), .in13(register_15_q),
    .in14(register_16_q), .in15(register_17_q), .out(B), .sel(multiplexer_1_out));
endmodule

module Control (
  input  [3:0] in_1,
  output PCSrc,
  output RegWrite,
  output ALUSrc,
  output MemoryWrite,
  output MemoryRead,
  output MemToReg,
  output Sll,
  output Binvert,
  output Lw_Sw,
  output [2:0] out_11
);

  wire decoder_1_out0, decoder_1_out1, decoder_1_out2, decoder_1_out3, decoder_1_out4, decoder_1_out5,
       decoder_1_out6, decoder_1_out7, decoder_1_out8, decoder_1_out9, decoder_1_out10, decoder_1_out11,
       decoder_1_out12, decoder_1_out13, decoder_1_out14, decoder_1_out15;

  r21 r21_1 (.A(in_1[3]), .B(in_1[2]), .C(in_1[1]), .D(in_1[0]), .X(out_11[2]), .Y(out_11[1]), .Z(out_11[0]));
  Decoder #(.select(4), .enable("false")) decoder_1 (
    .out0(decoder_1_out0), .out1(decoder_1_out1), .out2(decoder_1_out2), .out3(decoder_1_out3),
    .out4(decoder_1_out4), .out5(decoder_1_out5), .out6(decoder_1_out6), .out7(decoder_1_out7),
    .out8(decoder_1_out8), .out9(decoder_1_out9), .out10(decoder_1_out10), .out11(decoder_1_out11),
    .out12(decoder_1_out12), .out13(decoder_1_out13), .out14(decoder_1_out14), .out15(decoder_1_out15),
    .sel(in_1));
  or or_1 (PCSrc, decoder_1_out8, decoder_1_out8);
  or or_2 (RegWrite, decoder_1_out0, decoder_1_out1, decoder_1_out2, decoder_1_out4, decoder_1_out5, decoder_1_out6, decoder_1_out11);
  or or_3 (ALUSrc, decoder_1_out2, decoder_1_out6, decoder_1_out11, decoder_1_out12);
  or or_4 (MemoryWrite, decoder_1_out12, decoder_1_out12);
  or or_5 (MemoryRead, decoder_1_out11, decoder_1_out11);
  or or_6 (MemToReg, decoder_1_out0, decoder_1_out1, decoder_1_out2, decoder_1_out4, decoder_1_out5, decoder_1_out6);
  or u_Sll (Sll, decoder_1_out6, decoder_1_out6);
  or or_7 (Binvert, decoder_1_out8, decoder_1_out1);
  or or_8 (Lw_Sw, decoder_1_out12, decoder_1_out11);
endmodule

module r21 (
  input  A,
  input  B,
  input  C,
  input  D,
  output X,
  output Y,
  output Z
);

  wire and_2_out, and_3_out, not_1_out, not_2_out, not_3_out, not_4_out;

  not not_1 (not_1_out, A);
  and and_1 (Y, not_1_out, B);
  not not_2 (not_2_out, A);
  and and_2 (and_2_out, not_2_out, D);
  not not_3 (not_3_out, B);
  and and_3 (and_3_out, A, not_3_out, not_4_out);
  not not_4 (not_4_out, C);
  or or_1 (Z, and_2_out, and_3_out);

  assign X = 1'b0;
endmodule
