// Logisim project Registry File.circ as structural Verilog: 1 circuit, main circuit main
module main (
  input  Clock,
  input  Write_Register,
  input  [11:0] Write_Data,
  input  [3:0] Read_First,
  input  [3:0] Read_Second,
  input  [3:0] Select_Write,
  output [11:0] A,
  output [11:0] B,
  output [11:0] eqval,
  output [11:0] base
);

  wire and_1_out, and_2_out, and_3_out, and_4_out, and_5_out, and_6_out, and_7_out, and_8_out, and_9_out,
       and_10_out, and_11_out, and_12_out, and_13_out, and_14_out, and_15_out, and_16_out, decoder_1_out0,
       decoder_1_out1, decoder_1_out2, decoder_1_out3, decoder_1_out4, decoder_1_out5, decoder_1_out6,
       decoder_1_out7, decoder_1_out8, decoder_1_out9, decoder_1_out10, decoder_1_out11, decoder_1_out12,
       decoder_1_out13, decoder_1_out14, decoder_1_out15;
  wire [11:0] one_q, s0_q, s1_q, s2_q, s3_q, s4_q, s5_q, s6_q, t0_q, t1_q, t2_q, t3_q, t4_q, zero_q;

  Decoder #(.select(4), .enable("false")) decoder_1 (
    .out0(decoder_1_out0), .out1(decoder_1_out1), .out2(decoder_1_out2), .out3(decoder_1_out3),
    .out4(decoder_1_out4), .out5(decoder_1_out5), .out6(decoder_1_out6), .out7(decoder_1_out7),
    .out8(decoder_1_out8), .out9(decoder_1_out9), .out10(decoder_1_out10), .out11(decoder_1_out11),
    .out12(decoder_1_out12), .out13(decoder_1_out13), .out14(decoder_1_out14), .out15(decoder_1_out15),
    .sel(Select_Write));
  and and_1 (and_1_out, Write_Register, decoder_1_out0);
  and and_2 (and_2_out, Write_Register, decoder_1_out1);
  and and_3 (and_3_out, Write_Register, decoder_1_out2);
  and and_4 (and_4_out, Write_Register, decoder_1_out3);
  and and_5 (and_5_out, Write_Register, decoder_1_out4);
  and and_6 (and_6_out, Write_Register, decoder_1_out5);
  and and_7 (and_7_out, Write_Register, decoder_1_out6);
  and and_8 (and_8_out, Write_Register, decoder_1_out7);
  and and_9 (and_9_out, Write_Register, decoder_1_out8);
  and and_10 (and_10_out, Write_Register, decoder_1_out9);
  and and_11 (and_11_out, Write_Register, decoder_1_out10);
  and and_12 (and_12_out, Write_Register, decoder_1_out11);
  and and_13 (and_13_out, Write_Register, decoder_1_out12);
  and and_14 (and_14_out, Write_Register, decoder_1_out13);
  and and_15 (and_15_out, Write_Register, decoder_1_out14);
  and and_16 (and_16_out, Write_Register, decoder_1_out15);
  Register #(.width(12)) zero (.D(Write_Data), .en(and_1_out), .Q(zero_q), .clk(Clock));  // open: clr
  Register #(.width(12)) t0 (.D(Write_Data), .en(and_2_out), .Q(t0_q), .clk(Clock));  // open: clr
  Register #(.width(12)) t1 (.D(Write_Data), .en(and_3_out), .Q(t1_q), .clk(Clock));  // open: clr
  Register #(.width(12)) t2 (.D(Write_Data), .en(and_4_out), .Q(t2_q), .clk(Clock));  // open: clr
  Register #(.width(12)) t3 (.D(Write_Data), .en(and_5_out), .Q(t3_q), .clk(Clock));  // open: clr
  Register #(.width(12)) t4 (.D(Write_Data), .en(and_6_out), .Q(t4_q), .clk(Clock));  // open: clr
  Register #(.width(12)) s0 (.D(Write_Data), .en(and_7_out), .Q(s0_q), .clk(Clock));  // open: clr
  Register #(.width(12)) s1 (.D(Write_Data), .en(and_8_out), .Q(s1_q), .clk(Clock));  // open: clr
  Register #(.width(12)) s2 (.D(Write_Data), .en(and_9_out), .Q(s2_q), .clk(Clock));  // open: clr
  Register #(.width(12)) s3 (.D(Write_Data), .en(and_10_out), .Q(s3_q), .clk(Clock));  // open: clr
  Register #(.width(12)) s4 (.D(Write_Data), .en(and_11_out), .Q(s4_q), .clk(Clock));  // open: clr
  Register #(.width(12)) s5 (.D(Write_Data), .en(and_12_out), .Q(s5_q), .clk(Clock));  // open: clr
  Register #(.width(12)) s6 (.D(Write_Data), .en(and_13_out), .Q(s6_q), .clk(Clock));  // open: clr
  Register #(.width(12)) u_eqval (.D(Write_Data), .en(and_14_out), .Q(eqval), .clk(Clock));  // open: clr
  Register #(.width(12)) u_base (.D(Write_Data), .en(and_15_out), .Q(base), .clk(Clock));  // open: clr
  Register #(.width(12)) one (.D(Write_Data), .en(and_16_out), .Q(one_q), .clk(Clock));  // open: clr
  Multiplexer #(.select(4), .width(12), .enable("false")) multiplexer_1 (
    .in0(zero_q), .in1(t0_q), .in2(t1_q), .in3(t2_q), .in4(t3_q), .in5(t4_q), .in6(s0_q), .in7(s1_q),
    .in8(s2_q), .in9(s3_q), .in10(s4_q), .in11(s5_q), .in12(s6_q), .in13(eqval), .in14(base), .in15(one_q),
    .out(A), .sel(Read_First));
  Multiplexer #(.select(4), .width(12), .enable("false")) multiplexer_2 (
    .in0(zero_q), .in1(t0_q), .in2(t1_q), .in3(t2_q), .in4(t3_q), .in5(t4_q), .in6(s0_q), .in7(s1_q),
    .in8(s2_q), .in9(s3_q), .in10(s4_q), .in11(s5_q), .in12(s6_q), .in13(eqval), .in14(base), .in15(one_q),
    .out(B), .sel(Read_Second));
endmodule
