// Logisim project main.circ as structural Verilog: 1 circuit, main circuit main
module main (
  input  Clear,
  output [11:0] Output
);

  wire clock_1_out, main_1_first_oprand, main_1_write_register, main_1_zero_signal, not_1_out;
  wire [0:0] main_3_zero_signal_2;
  wire [1:0] main_1_branch, main_1_output, main_1_second_operand, main_1_write_read_memory;
  wire [2:0] main_1_alu_opcode;
  wire [11:0] adder_1_out, adder_2_out, adder_3_out, main_2_a, main_2_b, main_2_base, main_2_eqval,
       main_3_output, multiplexer_1_out, multiplexer_2_out, multiplexer_3_out, multiplexer_4_out, ram_1_data,
       register_1_q, rom_1_data;

  Multiplexer #(.select(2), .width(12), .enable("false")) multiplexer_1 (
    .in0(adder_2_out), .in1(multiplexer_4_out), .in2(adder_1_out), .in3(adder_1_out),
    .out(multiplexer_1_out), .sel(main_1_branch));
  Register #(.width(12)) register_1 (
    .D(multiplexer_1_out), .Q(register_1_q), .clk(clock_1_out), .clr(Clear));  // open: en
  ROM #(.addrWidth(12), .dataWidth(12)) rom_1 (.addr(register_1_q), .data(rom_1_data));  // open: sel
  Clock clock_1 (.out(clock_1_out));
  Control_Unit_main main_1 (
    .Opcode(rom_1_data[11:8]), .ALU_Opcode(main_1_alu_opcode), .Write_Register(main_1_write_register),
    .Branch(main_1_branch), .Write_Read_Memory(main_1_write_read_memory), .Zero_Signal(main_1_zero_signal),
    .Output(main_1_output), .First_Oprand(main_1_first_oprand), .Second_Operand(main_1_second_operand));
  Registry_File_main main_2 (
    .Clock(clock_1_out), .Write_Register(main_1_write_register), .Write_Data(Output),
    .Read_First(rom_1_data[7:4]), .Read_Second(rom_1_data[3:0]), .Select_Write(rom_1_data[7:4]),
    .A(main_2_a), .B(main_2_b), .eqval(main_2_eqval), .base(main_2_base));
  Multiplexer #(.width(12), .enable("false")) multiplexer_2 (
    .in0(main_2_a), .in1(main_2_base), .out(multiplexer_2_out), .sel(main_1_first_oprand));
  Multiplexer #(.select(2), .width(12), .enable("false")) multiplexer_3 (
    .in0(main_2_b), .in1(main_2_eqval), .in2({{8{1'b0}}, rom_1_data[3:0]}),
    .in3({{8{1'b0}}, rom_1_data[3:0]}), .out(multiplexer_3_out), .sel(main_1_second_operand));
  Adder #(.width(12)) adder_1 (
    .a({4'b0000, rom_1_data[7:0]}), .b(register_1_q), .out(adder_1_out), .cin(1'b0));  // open: cout
  Adder #(.width(12)) adder_2 (.a(register_1_q), .b({12{1'b0}}), .out(adder_2_out), .cin(1'b1));  // open: cout
  Adder #(.width(12)) adder_3 (
    .a(register_1_q), .b({{8{1'b0}}, rom_1_data[3:0]}), .out(adder_3_out));  // open: cin, cout
  Multiplexer #(.width(12), .enable("false")) multiplexer_4 (
    .in0(adder_2_out), .in1(adder_3_out), .out(multiplexer_4_out), .sel(main_3_zero_signal_2[0]));
  ALU_main main_3 (
    .ALU_Opcode(main_1_alu_opcode), .A(multiplexer_2_out), .B(multiplexer_3_out),
    .Zero_Signal(main_1_zero_signal), .Zero_Signal_2(main_3_zero_signal_2[0]), .Output(main_3_output));
  Multiplexer #(.select(2), .width(12), .enable("false")) multiplexer_5 (
    .in0(main_3_output), .in1({{11{1'b0}}, main_3_zero_signal_2[0]}), .in2(ram_1_data), .in3(ram_1_data),
    .out(Output), .sel(main_1_output));
  not not_1 (not_1_out, main_1_write_read_memory[0]);
  RAM #(.addrWidth(12), .dataWidth(12), .bus("separate")) ram_1 (
    .addr(main_3_output), .din(main_2_a), .data(ram_1_data), .str(not_1_out),
    .sel(main_1_write_read_memory[1]), .clk(clock_1_out), .ld(main_1_write_read_memory[0]));  // open: clr

  // Notes on the sheet:
  //   contents of rom_1 (hex, n*v repeats v):
  //   233 8ff 633 a31 a50 930 0 920
endmodule
